# Fritzing sketch tracktimer (saved by Fritzing 0.9.3b)

parts:
  Part5 = Arduino Pro Mini (3.3V)
  Grove1 = Grove 4 Digit Display
  8x8_LED_Modul_mit_MAX1 = 8x8 LED Modul mit MAX7219 [package=THT]
  8x8_LED_Modul_mit_MAX2 = 8x8 LED Modul mit MAX7219 [package=THT]
  8x8_LED_Modul_mit_MAX3 = 8x8 LED Modul mit MAX7219 [package=THT]
  8x8_LED_Modul_mit_MAX4 = 8x8 LED Modul mit MAX7219 [package=THT]
  Grove2 = Grove 4 Digit Display
  Grove3 = Grove 4 Digit Display
  Grove4 = Grove 4 Digit Display
  D2F1 = D2F-FL Omron Snap Action Limit Switch with Level
  Q1 = LTR-301 [package=ltr-301]
  Q2 = LTR-301 [package=ltr-301]
  Q3 = LTR-301 [package=ltr-301]
  Q4 = LTR-301 [package=ltr-301]

nets:
  VCC: Part5.VCC, Grove1.VCC, 8x8_LED_Modul_mit_MAX1.VCC_Eingang, Grove2.VCC, Grove3.VCC, Grove4.VCC, D2F1.NC
  GND: Part5.GND, Grove1.GND, 8x8_LED_Modul_mit_MAX1.GND_Eingang, Grove2.GND, Grove3.GND, Grove4.GND, D2F1.NO, Q1.E, Q2.E, Q3.E, Q4.E
  N1: Part5.A3, Q4.C
  N2: Part5.A2, Q3.C
  N3: Part5.A1, Q2.C
  N4: Part5.A0, Q1.C
  N5: Part5.SCK, D2F1.COM
  N6: Part5.MISO, 8x8_LED_Modul_mit_MAX1.DIN_Eingang
  N7: Part5.MOSI, 8x8_LED_Modul_mit_MAX1.CLK_Eingang
  N8: Part5.D10, 8x8_LED_Modul_mit_MAX1.CS_Eingang
  N9: Part5.D9, Grove4.DIO
  N10: Part5.D8, Grove4.CLK
  N11: Part5.D7, Grove3.DIO
  N12: Part5.D6, Grove3.CLK
  N13: Part5.D5, Grove2.DIO
  N14: Part5.D4, Grove2.CLK
  N15: Part5.D3, Grove1.DIO
  N16: Part5.D2, Grove1.CLK
  N17: 8x8_LED_Modul_mit_MAX1.VCC_Ausgang, 8x8_LED_Modul_mit_MAX2.VCC_Eingang
  N18: 8x8_LED_Modul_mit_MAX1.GND_Ausgang, 8x8_LED_Modul_mit_MAX2.GND_Eingang
  N19: 8x8_LED_Modul_mit_MAX1.DOUT_Ausgang, 8x8_LED_Modul_mit_MAX2.DIN_Eingang
  N20: 8x8_LED_Modul_mit_MAX1.CS_Ausgang, 8x8_LED_Modul_mit_MAX2.CS_Eingang
  N21: 8x8_LED_Modul_mit_MAX1.CLK_Ausgang, 8x8_LED_Modul_mit_MAX2.CLK_Eingang
  N22: 8x8_LED_Modul_mit_MAX2.VCC_Ausgang, 8x8_LED_Modul_mit_MAX3.VCC_Eingang
  N23: 8x8_LED_Modul_mit_MAX2.GND_Ausgang, 8x8_LED_Modul_mit_MAX3.GND_Eingang
  N24: 8x8_LED_Modul_mit_MAX2.DOUT_Ausgang, 8x8_LED_Modul_mit_MAX3.DIN_Eingang
  N25: 8x8_LED_Modul_mit_MAX2.CS_Ausgang, 8x8_LED_Modul_mit_MAX3.CS_Eingang
  N26: 8x8_LED_Modul_mit_MAX2.CLK_Ausgang, 8x8_LED_Modul_mit_MAX3.CLK_Eingang
  N27: 8x8_LED_Modul_mit_MAX3.VCC_Ausgang, 8x8_LED_Modul_mit_MAX4.VCC_Eingang
  N28: 8x8_LED_Modul_mit_MAX3.GND_Ausgang, 8x8_LED_Modul_mit_MAX4.GND_Eingang
  N29: 8x8_LED_Modul_mit_MAX3.DOUT_Ausgang, 8x8_LED_Modul_mit_MAX4.DIN_Eingang
  N30: 8x8_LED_Modul_mit_MAX3.CS_Ausgang, 8x8_LED_Modul_mit_MAX4.CS_Eingang
  N31: 8x8_LED_Modul_mit_MAX3.CLK_Ausgang, 8x8_LED_Modul_mit_MAX4.CLK_Eingang

custom parts:
  D2F-FL Omron Snap Action Limit Switch with Level: Snap action switch with stainless steel lever.
